// Logisim project CPU8bits.circ as structural Verilog
module main (
);

  wire AluSrc, clk, clock_1_out, control_1_conditional, control_1_jals, control_1_jump,
       control_1_returnadrress, ExitOn, FunctEn, MemToReg, MemWrite, not_1_out, not_2_out, not_3_out, RegDst,
       register_1_q, RegWrite;
  wire [1:0] control_1_jumpfunct;
  wire [2:0] multiplexer_4_out;
  wire [3:0] instjoin_1_out_3_2;
  wire [4:0] multiplexer_1_out, multiplexer_2_out;
  wire [7:0] alu_1_alurta, multiplexer_3_out, multiplexer_5_out, R1, R2, ram_1_dout, rom_1_data;
  wire [9:0] ADDRESS;
  wire [11:0] adder_1_out, counter_1_q, jmpcontrol_1_pcout;
  wire [19:10] instjoin_1_out_3;

  Clock clock_1 (.out(clock_1_out));
  assign clk = not_1_out ? clock_1_out : 1'bz;  // Controlled_Buffer controlled_buffer_1
  not not_1 (not_1_out, ExitOn);
  ROM #(.addrWidth(12)) rom_1 (.addr(counter_1_q), .data(rom_1_data));
  Counter #(.max('hfff), .width(12)) counter_1 (
    .load(1'b1), .D(jmpcontrol_1_pcout), .Q(counter_1_q), .clk(clk));  // open: count, carry, up, clr
  Hex_Digit_Display hex_digit_display_1 (.value(instjoin_1_out_3_2));  // open: dp
  Hex_Digit_Display hex_digit_display_2 (.value(instjoin_1_out_3[19:16]));  // open: dp
  Hex_Digit_Display hex_digit_display_3 (.value(instjoin_1_out_3[15:12]));  // open: dp
  Hex_Digit_Display hex_digit_display_4 (.value({instjoin_1_out_3[11:10], ADDRESS[9:8]}));  // open: dp
  Hex_Digit_Display hex_digit_display_5 (.value(ADDRESS[7:4]));  // open: dp
  Hex_Digit_Display hex_digit_display_6 (.value(ADDRESS[3:0]));  // open: dp
  Adder #(.width(12)) adder_1 (.a(12'h1), .b(counter_1_q), .out(adder_1_out));  // open: cin, cout
  INSTJOIN instjoin_1 (
    .INST1(rom_1_data), .CLK(clk), .out_3({instjoin_1_out_3_2, instjoin_1_out_3, ADDRESS}));  // open: clkout
  CONTROL control_1 (
    .OPCODE(instjoin_1_out_3_2), .JumpFunct(control_1_jumpfunct), .Conditional(control_1_conditional),
    .RegDst(RegDst), .JUMP(control_1_jump), .RegWrite(RegWrite), .AluSrc(AluSrc), .MemWrite(MemWrite),
    .MemToReg(MemToReg), .RETURNADRRESS(control_1_returnadrress), .functEnable(FunctEn),
    .JALS(control_1_jals), .EXITEN(ExitOn));
  Multiplexer #(.width(5)) multiplexer_1 (
    .in0(instjoin_1_out_3[19:15]), .in1(multiplexer_2_out), .out(multiplexer_1_out), .sel(not_2_out));
  Multiplexer #(.width(5)) multiplexer_2 (
    .in0(instjoin_1_out_3[14:10]), .in1(ADDRESS[9:5]), .out(multiplexer_2_out), .sel(RegDst));
  not not_2 (not_2_out, MemToReg);
  JMPCONTROL jmpcontrol_1 (
    .PC(adder_1_out), .ADDRESS(ADDRESS), .R1(R1), .RD(R2), .JUMPFUNCT(control_1_jumpfunct),
    .ENABLE(control_1_conditional), .JUMPENABLE(control_1_jump), .RET(control_1_returnadrress), .CLK(clk),
    .JAL(control_1_jals), .PCOUT(jmpcontrol_1_pcout));
  REGSFILE regsfile_1 (
    .RegWrite(RegWrite), .ReadReg1(instjoin_1_out_3[19:15]), .ReadReg2(instjoin_1_out_3[14:10]), .CLK(clk),
    .WriteRegister(multiplexer_1_out), .WriteData(multiplexer_5_out), .MemSignal(MemToReg), .ReadData1(R1),
    .ReadData2(R2));
  Multiplexer #(.width(8)) multiplexer_3 (.in0(R2), .in1(ADDRESS[7:0]), .out(multiplexer_3_out), .sel(AluSrc));
  Multiplexer #(.width(3)) multiplexer_4 (.in0(ADDRESS[2:0]), .in1(3'b000), .out(multiplexer_4_out), .sel(not_3_out));
  not not_3 (not_3_out, FunctEn);
  ALU alu_1 (.ALUSRC1(R1), .ALUSRC2(multiplexer_3_out), .FUNCT(multiplexer_4_out), .ALURTA(alu_1_alurta));
  RAM #(.addrWidth(15)) ram_1 (
    .addr({instjoin_1_out_3[14:10], ADDRESS}), .we(MemWrite), .oe(1'b1), .clk(clk), .din(R1),
    .dout(ram_1_dout));
  Multiplexer #(.width(8)) multiplexer_5 (
    .in0(alu_1_alurta), .in1(ram_1_dout), .out(multiplexer_5_out), .sel(register_1_q));
  Register #(.width(1)) register_1 (.D(MemToReg), .Q(register_1_q), .clk(clk));  // open: en, clr

  // Other names for the same wires on the sheet: CONST[7:0] = ADDRESS[7:0]

  // Notes on the sheet:
  //   contents of rom_1 (hex, n*v repeats v):
  //   40 4 1b 20 80 4 11 0 4 b0
  //   0x000000 NOP suma 0+0
  //   OPCODES
  //   0 TIPO O
  //   1 LD
  //   2 SD
  //   3 RET
  //   4 ADDI
  //   5 JMP
  //   6 JEQ
  //   7 JNE
  //   8 JLT
  //   9 JGT
  //   10 JAL
  //   INSTRUCCION
  //   INSTRUCTION ROM
  //   R1
  //   R2
  //   RD
  //   Funct
  //   const
endmodule

module CONTROL (
  input  [3:0] OPCODE,
  output [1:0] JumpFunct,
  output Conditional,
  output RegDst,
  output JUMP,
  output RegWrite,
  output AluSrc,
  output MemWrite,
  output MemToReg,
  output RETURNADRRESS,
  output functEnable,
  output JALS,
  output EXITEN
);

  wire ADDC_out, JEQ_out, JGT_out, JLT_out, JNE_out;

  Hex_Digit_Display hex_digit_display_1 (.value(OPCODE));  // open: dp
  and tipoO (functEnable, ~OPCODE[3], ~OPCODE[2], ~OPCODE[1], ~OPCODE[0]);  // AND_Gate
  and LD (MemToReg, ~OPCODE[3], ~OPCODE[2], ~OPCODE[1], OPCODE[0]);  // AND_Gate
  and SD (MemWrite, ~OPCODE[3], ~OPCODE[2], OPCODE[1], ~OPCODE[0]);  // AND_Gate
  and RET (RETURNADRRESS, ~OPCODE[3], ~OPCODE[2], OPCODE[1], OPCODE[0]);  // AND_Gate
  and ADDC (ADDC_out, ~OPCODE[3], OPCODE[2], ~OPCODE[1], ~OPCODE[0]);  // AND_Gate
  and JMP (JUMP, ~OPCODE[3], OPCODE[2], ~OPCODE[1], OPCODE[0]);  // AND_Gate
  and JEQ (JEQ_out, ~OPCODE[3], OPCODE[2], OPCODE[1], ~OPCODE[0]);  // AND_Gate
  and JNE (JNE_out, ~OPCODE[3], OPCODE[2], OPCODE[1], OPCODE[0]);  // AND_Gate
  and JLT (JLT_out, OPCODE[3], ~OPCODE[2], ~OPCODE[1], ~OPCODE[0]);  // AND_Gate
  and JGT (JGT_out, OPCODE[3], ~OPCODE[2], ~OPCODE[1], OPCODE[0]);  // AND_Gate
  and JAL (JALS, OPCODE[3], ~OPCODE[2], OPCODE[1], ~OPCODE[0]);  // AND_Gate
  and EXIT1 (EXITEN, OPCODE[3], ~OPCODE[2], OPCODE[1], OPCODE[0]);  // AND_Gate
  // AND_Gate and_1 is placed but not wired
  // AND_Gate and_2 is placed but not wired
  or or_1 (JumpFunct[0], JGT_out, JLT_out);
  or or_2 (JumpFunct[1], JNE_out, JGT_out);
  or or_3 (Conditional, JLT_out, JEQ_out, JNE_out, JGT_out);
  or or_4 (RegWrite, functEnable, MemToReg, ADDC_out);
  or or_5 (AluSrc, ADDC_out, MemToReg);

  assign RegDst = functEnable;
endmodule

module REGSFILE (
  input  RegWrite,
  input  [4:0] ReadReg1,
  input  [4:0] ReadReg2,
  input  CLK,
  input  [4:0] WriteRegister,
  input  [7:0] WriteData,
  input  MemSignal,
  output [7:0] ReadData1,
  output [7:0] ReadData2
);

  wire and_1_out, and_2_out, and_3_out, and_4_out, and_5_out, and_6_out, and_7_out, and_8_out, and_9_out,
       and_10_out, and_11_out, and_12_out, and_13_out, and_14_out, and_15_out, and_16_out, and_17_out,
       and_18_out, and_19_out, and_20_out, and_21_out, and_22_out, and_23_out, and_24_out, and_25_out,
       and_26_out, and_27_out, and_28_out, and_29_out, and_30_out, and_31_out, decoder_1_out1,
       decoder_1_out2, decoder_1_out3, decoder_1_out4, decoder_1_out5, decoder_1_out6, decoder_1_out7,
       decoder_1_out8, decoder_1_out9, decoder_1_out10, decoder_1_out11, decoder_1_out12, decoder_1_out13,
       decoder_1_out14, decoder_1_out15, decoder_1_out16, decoder_1_out17, decoder_1_out18, decoder_1_out19,
       decoder_1_out20, decoder_1_out21, decoder_1_out22, decoder_1_out23, decoder_1_out24, decoder_1_out25,
       decoder_1_out26, decoder_1_out27, decoder_1_out28, decoder_1_out29, decoder_1_out30, decoder_1_out31,
       register_1_q;
  wire [4:0] multiplexer_1_out, register_2_q;
  wire [7:0] R0_q, R1_q, R2_q, R3_q, R4_q, R5_q, R6_q, R7_q, R8_q, R9_q, R10_q, R11_q, R12_q, R13_q, R14_q,
       R15_q, R16_q, R17_q, R18_q, R19_q, R20_q, R21_q, R22_q, R23_q, R24_q, R25_q, R26_q, R27_q, R28_q,
       R29_q, R30_q, R31_q;

  Decoder #(.select(5)) decoder_1 (
    .out1(decoder_1_out1), .out2(decoder_1_out2), .out3(decoder_1_out3), .out4(decoder_1_out4),
    .out5(decoder_1_out5), .out6(decoder_1_out6), .out7(decoder_1_out7), .out8(decoder_1_out8),
    .out9(decoder_1_out9), .out10(decoder_1_out10), .out11(decoder_1_out11), .out12(decoder_1_out12),
    .out13(decoder_1_out13), .out14(decoder_1_out14), .out15(decoder_1_out15), .out16(decoder_1_out16),
    .out17(decoder_1_out17), .out18(decoder_1_out18), .out19(decoder_1_out19), .out20(decoder_1_out20),
    .out21(decoder_1_out21), .out22(decoder_1_out22), .out23(decoder_1_out23), .out24(decoder_1_out24),
    .out25(decoder_1_out25), .out26(decoder_1_out26), .out27(decoder_1_out27), .out28(decoder_1_out28),
    .out29(decoder_1_out29), .out30(decoder_1_out30), .out31(decoder_1_out31), .sel(multiplexer_1_out));  // open: out0, en
  Multiplexer #(.width(5)) multiplexer_1 (
    .in0(WriteRegister), .in1(register_2_q), .out(multiplexer_1_out), .sel(register_1_q));
  Register #(.width(1)) register_1 (.D(MemSignal), .en(1'b1), .Q(register_1_q), .clk(CLK));  // open: clr
  Register #(.width(5)) register_2 (.D(WriteRegister), .en(1'b1), .Q(register_2_q), .clk(CLK));  // open: clr
  and and_1 (and_1_out, decoder_1_out8, RegWrite);
  and and_2 (and_2_out, decoder_1_out16, RegWrite);
  and and_3 (and_3_out, decoder_1_out24, RegWrite);
  Register R0 (.D(WriteData), .en(1'b0), .Q(R0_q), .clk(CLK));  // open: clr
  Register R8 (.D(WriteData), .en(and_1_out), .Q(R8_q), .clk(CLK));  // open: clr
  Register R16 (.D(WriteData), .en(and_2_out), .Q(R16_q), .clk(CLK));  // open: clr
  Register R24 (.D(WriteData), .en(and_3_out), .Q(R24_q), .clk(CLK));  // open: clr
  Register R1 (.D(WriteData), .en(and_4_out), .Q(R1_q), .clk(CLK));  // open: clr
  and and_4 (and_4_out, decoder_1_out1, RegWrite);
  Register R9 (.D(WriteData), .en(and_5_out), .Q(R9_q), .clk(CLK));  // open: clr
  and and_5 (and_5_out, decoder_1_out9, RegWrite);
  Register R17 (.D(WriteData), .en(and_6_out), .Q(R17_q), .clk(CLK));  // open: clr
  and and_6 (and_6_out, decoder_1_out17, RegWrite);
  Register R25 (.D(WriteData), .en(and_7_out), .Q(R25_q), .clk(CLK));  // open: clr
  and and_7 (and_7_out, decoder_1_out25, RegWrite);
  and and_8 (and_8_out, decoder_1_out2, RegWrite);
  and and_9 (and_9_out, decoder_1_out10, RegWrite);
  and and_10 (and_10_out, decoder_1_out18, RegWrite);
  and and_11 (and_11_out, decoder_1_out26, RegWrite);
  Register R2 (.D(WriteData), .en(and_8_out), .Q(R2_q), .clk(CLK));  // open: clr
  Register R10 (.D(WriteData), .en(and_9_out), .Q(R10_q), .clk(CLK));  // open: clr
  Register R18 (.D(WriteData), .en(and_10_out), .Q(R18_q), .clk(CLK));  // open: clr
  Register R26 (.D(WriteData), .en(and_11_out), .Q(R26_q), .clk(CLK));  // open: clr
  Register R3 (.D(WriteData), .en(and_12_out), .Q(R3_q), .clk(CLK));  // open: clr
  and and_12 (and_12_out, decoder_1_out3, RegWrite);
  Register R11 (.D(WriteData), .en(and_13_out), .Q(R11_q), .clk(CLK));  // open: clr
  and and_13 (and_13_out, decoder_1_out11, RegWrite);
  Register R19 (.D(WriteData), .en(and_14_out), .Q(R19_q), .clk(CLK));  // open: clr
  and and_14 (and_14_out, decoder_1_out19, RegWrite);
  Register R27 (.D(WriteData), .en(and_15_out), .Q(R27_q), .clk(CLK));  // open: clr
  and and_15 (and_15_out, decoder_1_out27, RegWrite);
  and and_16 (and_16_out, decoder_1_out4, RegWrite);
  and and_17 (and_17_out, decoder_1_out12, RegWrite);
  and and_18 (and_18_out, decoder_1_out20, RegWrite);
  and and_19 (and_19_out, decoder_1_out28, RegWrite);
  Register R4 (.D(WriteData), .en(and_16_out), .Q(R4_q), .clk(CLK));  // open: clr
  Register R12 (.D(WriteData), .en(and_17_out), .Q(R12_q), .clk(CLK));  // open: clr
  Register R20 (.D(WriteData), .en(and_18_out), .Q(R20_q), .clk(CLK));  // open: clr
  Register R28 (.en(and_19_out), .Q(R28_q), .clk(CLK));  // open: D, clr
  and and_20 (and_20_out, decoder_1_out5, RegWrite);
  and and_21 (and_21_out, decoder_1_out13, RegWrite);
  and and_22 (and_22_out, decoder_1_out21, RegWrite);
  and and_23 (and_23_out, decoder_1_out29, RegWrite);
  Register R5 (.D(WriteData), .en(and_20_out), .Q(R5_q), .clk(CLK));  // open: clr
  and and_24 (and_24_out, decoder_1_out6, RegWrite);
  Register R13 (.D(WriteData), .en(and_21_out), .Q(R13_q), .clk(CLK));  // open: clr
  and and_25 (and_25_out, decoder_1_out14, RegWrite);
  Register R21 (.D(WriteData), .en(and_22_out), .Q(R21_q), .clk(CLK));  // open: clr
  and and_26 (and_26_out, decoder_1_out22, RegWrite);
  Register R29 (.D(WriteData), .en(and_23_out), .Q(R29_q), .clk(CLK));  // open: clr
  and and_27 (and_27_out, decoder_1_out30, RegWrite);
  Register R6 (.D(WriteData), .en(and_24_out), .Q(R6_q));  // open: clk, clr
  Register R14 (.D(WriteData), .en(and_25_out), .Q(R14_q), .clk(CLK));  // open: clr
  Register R22 (.D(WriteData), .en(and_26_out), .Q(R22_q), .clk(CLK));  // open: clr
  Register R30 (.D(WriteData), .en(and_27_out), .Q(R30_q), .clk(CLK));  // open: clr
  and and_28 (and_28_out, decoder_1_out7, RegWrite);
  and and_29 (and_29_out, decoder_1_out15, RegWrite);
  and and_30 (and_30_out, decoder_1_out23, RegWrite);
  and and_31 (and_31_out, decoder_1_out31, RegWrite);
  Register R7 (.D(WriteData), .en(and_28_out), .Q(R7_q));  // open: clk, clr
  Register R15 (.D(WriteData), .en(and_29_out), .Q(R15_q), .clk(CLK));  // open: clr
  Register R23 (.D(WriteData), .en(and_30_out), .Q(R23_q));  // open: clk, clr
  Register R31 (.D(WriteData), .en(and_31_out), .Q(R31_q), .clk(CLK));  // open: clr
  Multiplexer #(.select(5), .width(8)) multiplexer_2 (
    .in0(R0_q), .in1(R1_q), .in2(R2_q), .in3(R3_q), .in4(R4_q), .in5(R5_q), .in6(R6_q), .in7(R7_q),
    .in8(R8_q), .in9(R9_q), .in10(R10_q), .in11(R11_q), .in12(R12_q), .in13(R13_q), .in14(R14_q),
    .in15(R15_q), .in16(R16_q), .in17(R17_q), .in18(R18_q), .in19(R19_q), .in20(R20_q), .in21(R21_q),
    .in22(R22_q), .in23(R23_q), .in24(R24_q), .in25(R25_q), .in26(R26_q), .in27(R27_q), .in28(R28_q),
    .in29(R29_q), .in30(R30_q), .in31(R31_q), .out(ReadData1), .sel(ReadReg1));
  Multiplexer #(.select(5), .width(8)) multiplexer_3 (
    .in0(R0_q), .in1(R1_q), .in2(R2_q), .in3(R3_q), .in4(R4_q), .in5(R5_q), .in6(R6_q), .in7(R7_q),
    .in8(R8_q), .in9(R9_q), .in10(R10_q), .in11(R11_q), .in12(R12_q), .in13(R13_q), .in14(R14_q),
    .in15(R15_q), .in16(R16_q), .in17(R17_q), .in18(R18_q), .in19(R19_q), .in20(R20_q), .in21(R21_q),
    .in22(R22_q), .in23(R23_q), .in24(R24_q), .in25(R25_q), .in26(R26_q), .in27(R27_q), .in28(R28_q),
    .in29(R29_q), .in30(R30_q), .in31(R31_q), .out(ReadData2), .sel(ReadReg2));

  // Other names for the same wires on the sheet: RR1[4:0] = ReadReg1; RR2[4:0] = ReadReg2
endmodule

module ALU (
  input  [7:0] ALUSRC1,
  input  [7:0] ALUSRC2,
  input  [2:0] FUNCT,
  output [7:0] ALURTA
);

  wire [7:0] adder_1_out, and_1_out, divider_1_out, multiplier_1_out, nand_1_out, or_1_out, subtractor_1_out,
       xor_1_out;

  // Shift_Register shift_register_1: pin names not known
  Adder adder_1 (.a(ALUSRC1), .b(ALUSRC2), .out(adder_1_out));  // open: cin, cout
  Subtractor subtractor_1 (.a(ALUSRC1), .b(ALUSRC2), .out(subtractor_1_out));  // open: bin, bout
  Multiplier multiplier_1 (.a(ALUSRC1), .b(ALUSRC2), .out(multiplier_1_out));  // open: cin, cout
  Divider divider_1 (.a(ALUSRC1), .b(ALUSRC2), .out(divider_1_out));  // open: upper, rem
  assign and_1_out = ALUSRC1 & ALUSRC2;  // AND_Gate and_1, 8 bits wide
  assign or_1_out = ALUSRC1 | ALUSRC2;  // OR_Gate or_1, 8 bits wide
  assign xor_1_out = ALUSRC1 ^ ALUSRC2;  // XOR_Gate xor_1, 8 bits wide
  assign nand_1_out = ~(ALUSRC1 & ALUSRC2);  // NAND_Gate nand_1, 8 bits wide
  // NOR_Gate nor_1 has open pins: in0=ALUSRC1, in1=ALUSRC2, out=open
  // XNOR_Gate xnor_1 has open pins: in0=ALUSRC1, in1=ALUSRC2, out=open
  Multiplexer #(.select(3), .width(8)) multiplexer_1 (
    .in0(adder_1_out), .in1(subtractor_1_out), .in2(multiplier_1_out), .in3(divider_1_out), .in4(and_1_out),
    .in5(or_1_out), .in6(xor_1_out), .in7(nand_1_out), .out(ALURTA), .sel(FUNCT));
  Hex_Digit_Display hex_digit_display_1 (.value(ALURTA[7:4]));  // open: dp
  Hex_Digit_Display hex_digit_display_2 (.value(ALURTA[3:0]));  // open: dp
endmodule

module JMPCONTROL (
  input  [11:0] PC,
  input  [9:0] ADDRESS,
  input  [7:0] R1,
  input  [7:0] RD,
  input  [1:0] JUMPFUNCT,
  input  ENABLE,
  input  JUMPENABLE,
  input  RET,
  input  CLK,
  input  JAL,
  output [11:0] PCOUT
);

  wire comparator_1_eq, comparator_1_gt, comparator_1_lt, condition_out, multiplexer_1_out, not_1_out,
       or_1_out;
  wire [11:0] bit_extender_1_out, multiplexer_2_out, RA_q;

  Comparator comparator_1 (.a(R1), .b(RD), .gt(comparator_1_gt), .eq(comparator_1_eq), .lt(comparator_1_lt));
  not not_1 (not_1_out, comparator_1_eq);
  Multiplexer #(.select(2)) multiplexer_1 (
    .in0(comparator_1_eq), .in1(not_1_out), .in2(comparator_1_lt), .in3(comparator_1_gt),
    .out(multiplexer_1_out), .sel(JUMPFUNCT));
  assign bit_extender_1_out = {{2{ADDRESS[9]}}, ADDRESS};  // Bit_Extender bit_extender_1
  and condition (condition_out, multiplexer_1_out, ENABLE);
  or or_1 (or_1_out, JAL, condition_out, JUMPENABLE);
  Register #(.width(12)) RA (.D(PC), .en(JAL), .Q(RA_q), .clk(CLK));  // open: clr
  Multiplexer #(.width(12)) multiplexer_2 (.in0(PC), .in1(bit_extender_1_out), .out(multiplexer_2_out), .sel(or_1_out));
  Multiplexer #(.width(12)) multiplexer_3 (.in0(multiplexer_2_out), .in1(RA_q), .out(PCOUT), .sel(RET));

  // Other names for the same wires on the sheet: Disable1 = ENABLE; jmpandlink = JAL; unconditional = JUMPENABLE
endmodule

module INSTJOIN (
  input  [7:0] INST1,
  input  CLK,
  output [23:0] out_3,
  output clkout
);

  wire decoder_1_out0, decoder_1_out1, not_1_out;
  wire [1:0] counter_1_q;
  wire [7:0] register_1_q, register_2_q;

  Counter #(.max('h2), .width(2)) counter_1 (.Q(counter_1_q), .clk(CLK));  // open: load, D, count, carry, up, clr
  Decoder #(.select(2)) decoder_1 (
    .out0(decoder_1_out0), .out1(decoder_1_out1), .out2(clkout), .sel(counter_1_q));  // open: out3, en
  Register #(.trigger("falling")) register_1 (.D(INST1), .Q(register_1_q), .clk(decoder_1_out0));  // open: en, clr
  Register #(.trigger("falling")) register_2 (.D(INST1), .Q(register_2_q), .clk(decoder_1_out1));  // open: en, clr
  Multiplexer #(.width(24)) multiplexer_1 (
    .in0({register_1_q, register_2_q, INST1}), .in1({24{1'b0}}), .out(out_3), .sel(not_1_out));
  not not_1 (not_1_out, clkout);
endmodule
