// Logisim project asd.circ as structural Verilog: 7 circuits, main circuit main
module main (
  output [15:0] out_1
);

  wire AluSrc, clk, clock_1_out, control_1_conditional, control_1_jals, control_1_jump,
       control_1_returnadrress, ExitOn, FunctEn, MemToReg, MemWrite, not_1_out, not_2_out, RegDst, RegWrite,
       stop;
  wire [1:0] control_1_jumpfunct;
  wire [2:0] multiplexer_1_out, multiplexer_3_out;
  wire [7:0] adder_1_out, alu_1_alurta, CONST, counter_1_q, jmpcontrol_1_pcout, multiplexer_2_out,
       multiplexer_4_out, R1, ram_1_dout, RD, rom_1_data;

  Clock clock_1 (.out(clock_1_out));
  assign clk = not_1_out ? clock_1_out : 1'bz;  // Controlled_Buffer controlled_buffer_1
  not not_1 (not_1_out, stop);
  ROM rom_1 (.addr(counter_1_q), .data(rom_1_data));
  Counter counter_1 (.load(1'b1), .D(jmpcontrol_1_pcout), .Q(counter_1_q), .clk(clk));  // open: count, carry, up, clr
  Hex_Digit_Display hex_digit_display_1 (.value(out_1[15:12]));  // open: dp
  Adder adder_1 (.a(8'h1), .b(counter_1_q), .out(adder_1_out));  // open: cin, cout
  INSTCONTROL instcontrol_1 (.INST1(rom_1_data), .CLK(clk), .out_3(out_1));
  CONTROL control_1 (
    .OPCODE(out_1[15:12]), .JumpFunct(control_1_jumpfunct), .Conditional(control_1_conditional),
    .RegDst(RegDst), .JUMP(control_1_jump), .RegWrite(RegWrite), .AluSrc(AluSrc), .MemWrite(MemWrite),
    .MemToReg(MemToReg), .RETURNADRRESS(control_1_returnadrress), .functEnable(FunctEn),
    .JALS(control_1_jals), .EXITEN(ExitOn));
  Multiplexer #(.width(3)) multiplexer_1 (.in0(out_1[8:6]), .in1(out_1[5:3]), .out(multiplexer_1_out), .sel(RegDst));
  assign CONST = {{2{out_1[5]}}, out_1[5:0]};  // Bit_Extender bit_extender_1
  JMPCONTROL jmpcontrol_1 (
    .PC(adder_1_out), .CONST(CONST), .ADDRESS(out_1[7:0]), .R1(R1), .RD(RD), .JUMPFUNCT(control_1_jumpfunct),
    .ENABLE(control_1_conditional), .JUMPENABLE(control_1_jump), .RET(control_1_returnadrress), .CLK(clk),
    .JAL(control_1_jals), .PCOUT(jmpcontrol_1_pcout));
  REGSFILE regsfile_1 (
    .RegWrite(RegWrite), .ReadReg1(out_1[11:9]), .ReadReg2(out_1[8:6]), .CLK(clk),
    .WriteRegister(multiplexer_1_out), .WriteData(multiplexer_4_out), .ReadData1(R1), .ReadData2(RD));
  Multiplexer #(.width(8)) multiplexer_2 (.in0(RD), .in1(CONST), .out(multiplexer_2_out), .sel(AluSrc));
  Multiplexer #(.width(3)) multiplexer_3 (.in0(out_1[2:0]), .in1(3'b000), .out(multiplexer_3_out), .sel(not_2_out));
  not not_2 (not_2_out, FunctEn);
  SYSCALLS syscalls_1 (.SyscallSign(ExitOn), .syscallconst(out_1[3:0]), .STOPCLK(stop));
  ALU alu_1 (.ALUSRC1(R1), .ALUSRC2(multiplexer_2_out), .FUNCT(multiplexer_3_out), .ALURTA(alu_1_alurta));
  RAM ram_1 (.addr(CONST), .we(MemWrite), .oe(1'b1), .clk(clk), .din(R1), .dout(ram_1_dout));
  Multiplexer #(.width(8)) multiplexer_4 (
    .in0(alu_1_alurta), .in1(ram_1_dout), .out(multiplexer_4_out), .sel(MemToReg));

  // Other names for the same wires on the sheet: ADDRESS[7:0] = out_1[7:0]; SysAddr[3:0] = out_1[3:0]

  // Notes on the sheet:
  //   contents of rom_1 (hex, n*v repeats v):
  //   40 45 40 c1 40 81 42 41 a0 c b0 0 62 94 6 9a 44 81 50 c 30
  //   OPCODES
  //   0 TIPO O
  //   1 LD
  //   2 SD
  //   3 RET
  //   4 ADDI
  //   5 JMP
  //   6 JEQ
  //   7 JNE
  //   8 JLT
  //   9 JGT
  //   10 JAL
  //   INSTRUCTION ROM
  //   OPCODE
  //   R1
  //   R2
  //   RD
  //   Funct
  //   const
endmodule

module CONTROL (
  input  [3:0] OPCODE,
  output [1:0] JumpFunct,
  output Conditional,
  output RegDst,
  output JUMP,
  output RegWrite,
  output AluSrc,
  output MemWrite,
  output MemToReg,
  output RETURNADRRESS,
  output functEnable,
  output JALS,
  output EXITEN
);

  wire ADDC_out, JEQ_out, JGT_out, JLT_out, JNE_out;

  and tipoO (functEnable, ~OPCODE[3], ~OPCODE[2], ~OPCODE[1], ~OPCODE[0]);  // AND_Gate
  and LD (MemToReg, ~OPCODE[3], ~OPCODE[2], ~OPCODE[1], OPCODE[0]);  // AND_Gate
  and SD (MemWrite, ~OPCODE[3], ~OPCODE[2], OPCODE[1], ~OPCODE[0]);  // AND_Gate
  and RET (RETURNADRRESS, ~OPCODE[3], ~OPCODE[2], OPCODE[1], OPCODE[0]);  // AND_Gate
  and ADDC (ADDC_out, ~OPCODE[3], OPCODE[2], ~OPCODE[1], ~OPCODE[0]);  // AND_Gate
  and JMP (JUMP, ~OPCODE[3], OPCODE[2], ~OPCODE[1], OPCODE[0]);  // AND_Gate
  and JEQ (JEQ_out, ~OPCODE[3], OPCODE[2], OPCODE[1], ~OPCODE[0]);  // AND_Gate
  and JNE (JNE_out, ~OPCODE[3], OPCODE[2], OPCODE[1], OPCODE[0]);  // AND_Gate
  and JLT (JLT_out, OPCODE[3], ~OPCODE[2], ~OPCODE[1], ~OPCODE[0]);  // AND_Gate
  and JGT (JGT_out, OPCODE[3], ~OPCODE[2], ~OPCODE[1], OPCODE[0]);  // AND_Gate
  and JAL (JALS, OPCODE[3], ~OPCODE[2], OPCODE[1], ~OPCODE[0]);  // AND_Gate
  and EXIT1 (EXITEN, OPCODE[3], ~OPCODE[2], OPCODE[1], OPCODE[0]);  // AND_Gate
  // AND_Gate and_1 is placed but not wired
  // AND_Gate and_2 is placed but not wired
  or or_1 (JumpFunct[0], JGT_out, JLT_out);
  or or_2 (JumpFunct[1], JNE_out, JGT_out);
  or or_3 (Conditional, JLT_out, JEQ_out, JNE_out, JGT_out);
  or or_4 (RegWrite, functEnable, MemToReg, ADDC_out);
  or or_5 (AluSrc, ADDC_out, MemToReg);

  assign RegDst = functEnable;
endmodule

module REGSFILE (
  input  RegWrite,
  input  [2:0] ReadReg1,
  input  [2:0] ReadReg2,
  input  CLK,
  input  [2:0] WriteRegister,
  input  [7:0] WriteData,
  output [7:0] ReadData1,
  output [7:0] ReadData2
);

  wire and_1_out, and_2_out, and_3_out, and_4_out, and_5_out, and_6_out, and_7_out, decoder_1_out1,
       decoder_1_out2, decoder_1_out3, decoder_1_out4, decoder_1_out5, decoder_1_out6, decoder_1_out7;
  wire [7:0] R0_q, R1_q, R2_q, R3_q, R4_q, R5_q, R6_q, R7_q;

  Decoder #(.select(3)) decoder_1 (
    .out1(decoder_1_out1), .out2(decoder_1_out2), .out3(decoder_1_out3), .out4(decoder_1_out4),
    .out5(decoder_1_out5), .out6(decoder_1_out6), .out7(decoder_1_out7), .sel(WriteRegister));  // open: out0, en
  and and_1 (and_1_out, RegWrite, decoder_1_out1);
  Register R0 (.D(WriteData), .en(1'b0), .Q(R0_q), .clk(CLK));  // open: clr
  Register R1 (.D(WriteData), .en(and_1_out), .Q(R1_q), .clk(CLK));  // open: clr
  and and_2 (and_2_out, RegWrite, decoder_1_out2);
  and and_3 (and_3_out, RegWrite, decoder_1_out3);
  Register R2 (.D(WriteData), .en(and_2_out), .Q(R2_q), .clk(CLK));  // open: clr
  Register R3 (.D(WriteData), .en(and_3_out), .Q(R3_q), .clk(CLK));  // open: clr
  and and_4 (and_4_out, RegWrite, decoder_1_out4);
  and and_5 (and_5_out, RegWrite, decoder_1_out5);
  Register R4 (.D(WriteData), .en(and_4_out), .Q(R4_q), .clk(CLK));  // open: clr
  Register R5 (.D(WriteData), .en(and_5_out), .Q(R5_q), .clk(CLK));  // open: clr
  and and_6 (and_6_out, RegWrite, decoder_1_out6);
  and and_7 (and_7_out, RegWrite, decoder_1_out7);
  Register R6 (.D(WriteData), .en(and_6_out), .Q(R6_q), .clk(CLK));  // open: clr
  Register R7 (.D(WriteData), .en(and_7_out), .Q(R7_q), .clk(CLK));  // open: clr
  Multiplexer #(.select(3), .width(8)) multiplexer_1 (
    .in0(R0_q), .in1(R1_q), .in2(R2_q), .in3(R3_q), .in4(R4_q), .in5(R5_q), .in6(R6_q), .in7(R7_q),
    .out(ReadData1), .sel(ReadReg1));
  Multiplexer #(.select(3), .width(8)) multiplexer_2 (
    .in0(R0_q), .in1(R1_q), .in2(R2_q), .in3(R3_q), .in4(R4_q), .in5(R5_q), .in6(R6_q), .in7(R7_q),
    .out(ReadData2), .sel(ReadReg2));

  // Other names for the same wires on the sheet: RR1[2:0] = ReadReg1; RR2[2:0] = ReadReg2
endmodule

module ALU (
  input  [7:0] ALUSRC1,
  input  [7:0] ALUSRC2,
  input  [2:0] FUNCT,
  output [7:0] ALURTA
);

  wire [7:0] adder_1_out, and_1_out, divider_1_out, multiplier_1_out, nand_1_out, or_1_out, subtractor_1_out,
       xor_1_out;

  Adder adder_1 (.a(ALUSRC1), .b(ALUSRC2), .out(adder_1_out));  // open: cin, cout
  Subtractor subtractor_1 (.a(ALUSRC1), .b(ALUSRC2), .out(subtractor_1_out));  // open: bin, bout
  Multiplier multiplier_1 (.a(ALUSRC1), .b(ALUSRC2), .out(multiplier_1_out));  // open: cin, cout
  Divider divider_1 (.a(ALUSRC1), .b(ALUSRC2), .out(divider_1_out));  // open: upper, rem
  assign and_1_out = ALUSRC1 & ALUSRC2;  // AND_Gate and_1, 8 bits wide
  assign or_1_out = ALUSRC1 | ALUSRC2;  // OR_Gate or_1, 8 bits wide
  assign xor_1_out = ALUSRC1 ^ ALUSRC2;  // XOR_Gate xor_1, 8 bits wide
  assign nand_1_out = ~(ALUSRC1 & ALUSRC2);  // NAND_Gate nand_1, 8 bits wide
  Multiplexer #(.select(3), .width(8)) multiplexer_1 (
    .in0(adder_1_out), .in1(subtractor_1_out), .in2(multiplier_1_out), .in3(divider_1_out), .in4(and_1_out),
    .in5(or_1_out), .in6(xor_1_out), .in7(nand_1_out), .out(ALURTA), .sel(FUNCT));
endmodule

module JMPCONTROL (
  input  [7:0] PC,
  input  [7:0] CONST,
  input  [7:0] ADDRESS,
  input  [7:0] R1,
  input  [7:0] RD,
  input  [1:0] JUMPFUNCT,
  input  ENABLE,
  input  JUMPENABLE,
  input  RET,
  input  CLK,
  input  JAL,
  output [7:0] PCOUT
);

  wire condition_out, GREATHER, LESS, multiplexer_1_out, not_1_out, or_1_out, ZERO;
  wire [7:0] multiplexer_2_out, multiplexer_3_out, RA_q;

  Comparator comparator_1 (.a(R1), .b(RD), .gt(GREATHER), .eq(ZERO), .lt(LESS));
  not not_1 (not_1_out, ZERO);
  Multiplexer #(.select(2)) multiplexer_1 (
    .in0(ZERO), .in1(not_1_out), .in2(LESS), .in3(GREATHER), .out(multiplexer_1_out), .sel(JUMPFUNCT));
  Multiplexer #(.width(8)) multiplexer_2 (.in0(PC), .in1(CONST), .out(multiplexer_2_out), .sel(condition_out));
  and condition (condition_out, multiplexer_1_out, ENABLE);
  or or_1 (or_1_out, JAL, JUMPENABLE);
  Register RA (.D(PC), .en(JAL), .Q(RA_q), .clk(CLK));  // open: clr
  Multiplexer #(.width(8)) multiplexer_3 (
    .in0(multiplexer_2_out), .in1(ADDRESS), .out(multiplexer_3_out), .sel(or_1_out));
  Multiplexer #(.width(8)) multiplexer_4 (.in0(multiplexer_3_out), .in1(RA_q), .out(PCOUT), .sel(RET));

  // Other names for the same wires on the sheet: Disable1 = ENABLE; unconditional = JUMPENABLE
endmodule

module INSTCONTROL (
  input  [7:0] INST1,
  input  CLK,
  output [15:0] out_3
);

  wire counter_1_carry, not_1_out, not_2_out;
  wire [7:0] register_1_q;

  Register #(.trigger("falling")) register_1 (.D(INST1), .Q(register_1_q), .clk(not_1_out));  // open: en, clr
  not not_1 (not_1_out, CLK);
  Counter #(.max('h1), .width(2)) counter_1 (.carry(counter_1_carry), .clk(CLK));  // open: load, D, count, Q, up, clr
  Multiplexer #(.width(16)) multiplexer_1 (.in0({register_1_q, INST1}), .in1({16{1'b0}}), .out(out_3), .sel(not_2_out));
  not not_2 (not_2_out, counter_1_carry);
endmodule

module SYSCALLS (
  input  SyscallSign,
  input  [3:0] syscallconst,
  output STOPCLK
);

  Decoder #(.select(4)) decoder_1 (
    .out0(STOPCLK), .sel(syscallconst), .en(SyscallSign));  // open: out1, out2, out3, out4, out5, out6, out7, out8, out9, out10, out11, out12, out13, out14, out15
endmodule
